# Fritzing sketch LVDCschematicV5 (saved by Fritzing 0.9.6b)

parts:
  Part1 = Arduino Nano (Rev3.0)
  S1 = Pushbutton [package="[THT]"]
  Buck_Convertor1 = Buck Convertor [part_number=LM2596 package=THT]
  J1 = Screw terminal - 2 pins [package=THT]
  R3 = Resistor [tolerance=±5% power=0.25 resistance=220 package=THT]
  R4 = Resistor [tolerance=±5% power=0.25 resistance=220 package=THT]
  R5 = Resistor [tolerance=±5% power=0.25 resistance=10k package=THT]
  LCM1602_IIC1 = LCM1602 IIC [part_number="LCM1602 IIC" chip_label="LCM1602 IIC" package="DIP (Dual Inline) [THT]"]
  LCD1 = LCD screen
  M1 = 1 chan 5v relay module
  RY1 = SSR-40VA
  J2 = Screw terminal - 2 pins [package=THT]
  RE1 = KY-040 Rotary encoder [package=THT]
  BAT1 = 12 battery [package=battery]

nets:
  GND: Part1.GND, Buck_Convertor1.Negative_Output, R3.Pin_1, R5.Pin_0, LCM1602_IIC1.GND, RE1.GND
  N1: Part1.D2, M1.pin_3
  N2: Part1.D6, RE1.CLK
  N3: Part1.D7, RE1.DT
  N4: Part1.D8, RE1.SW
  N5: Part1.D9, S1.Pin_1, S1.Pin_2, R5.Pin_1
  N6: Part1.VIN, S1.Pin_3, S1.Pin_4, Buck_Convertor1.Positive_Output, M1.pin_5
  VCC: Part1.5V, LCM1602_IIC1.VCC, RE1.Vcc
  N7: Part1.A5, LCM1602_IIC1.SCL
  N8: Part1.A4, LCM1602_IIC1.SDA
  N9: Part1.A0, R3.Pin_0, R4.Pin_1
  N10: Buck_Convertor1.Negative_Input, J1.pin2
  N11: J1.pin1, RY1.Pin_2
  VSS: LCM1602_IIC1.VSS, LCD1.VSS
  VDD: LCM1602_IIC1.VDD, LCD1.VDD
  N12: LCM1602_IIC1.V0, LCD1.V0
  N13: LCM1602_IIC1.RS, LCD1.RS
  N14: LCM1602_IIC1.RW, LCD1.R/W
  N15: LCM1602_IIC1.E, LCD1.E
  N16: LCM1602_IIC1.D0, LCD1.DB0
  N17: LCM1602_IIC1.D1, LCD1.DB1
  N18: LCM1602_IIC1.D2, LCD1.DB2
  N19: LCM1602_IIC1.D3, LCD1.DB3
  N20: LCM1602_IIC1.D4, LCD1.DB4
  N21: LCM1602_IIC1.D5, LCD1.DB5
  N22: LCM1602_IIC1.D6, LCD1.DB6
  N23: LCM1602_IIC1.D7, LCD1.DB7
  N24: LCM1602_IIC1.A, LCD1.LED+
  N25: LCM1602_IIC1.K, LCD1.LED-
  N26: M1.pin_4, RY1.Pin_3
  N27: J2.pin1, BAT1.+
  N28: J2.pin2, BAT1.-

notes:
  Voltage Sensor
  1 Channel Relay
  Buck Converter
  12V to 5V Step Down
  Circuit Breaker
  3-32 Solid State Relay
  12 Volt - 100Ah Batteries (48V)
  48 Volt Terminal
  10k Pull Down
  Arduino Nano
  ESP32

custom parts:
  Buck Convertor: DC to DC buck convertor
  LCM1602 IIC: I2C-Module to use a 1602 or 2004 LCD on with the wire.h libory Serial LCD Modul
  1 chan 5v relay module: 1 Channel 5V Relay Module Board Shield with Optocoupler Support High and Low Level Trigger for Arduino.
  SSR-40VA: SSR-40VA solid state relay.
  KY-040 Rotary encoder: KY-040 Rotary Encoder with switch on breakout borad from AZ Delivery
  12 battery: 12V lead acid type battery, like the Husqvarna YTH2448 12V 35AH battery. The pads in pcb are sized to accomidate up to 14ga wire (as these batterys will deliver high currents.)

// code stored in the sketch: 12September2023.ino
#include <LiquidCrystal.h>

// Initialize the LCD library with the numbers of the interface pins
LiquidCrystal lcd(12, 11, 5, 4, 3, 2);

// Define the number of menu options and initialize the menu items
const int numOptions = 4;
const char* menuOptions[numOptions] = {
  "Option 1",
  "Option 2",
  "Option 3",
  "Option 4"
};

// Initialize variables for menu navigation
int selectedOption = 0;
bool optionSelected = false;

void setup() {
  // Initialize the LCD
  lcd.begin(16, 2);

  // Display the initial menu
  displayMenu();
}

void loop() {
  // Check for button presses and update the selected option
  if (digitalRead(A0) == LOW) {
    delay(200); // Debounce delay
    selectedOption = (selectedOption + 1) % numOptions;
    displayMenu();
  }

  if (digitalRead(A1) == LOW) {
    delay(200); // Debounce delay
    optionSelected = true;
  }

  // If an option is selected, perform the corresponding action
  if (optionSelected) {
    lcd.clear();
    lcd.setCursor(0, 0);
    lcd.print("Selected: ");
    lcd.print(menuOptions[selectedOption]);
    // You can perform an action related to the selected option here
    delay(2000); // Display for 2 seconds
    optionSelected = false;
    displayMenu();
  }
}

void displayMenu() {
  lcd.clear();
  lcd.setCursor(0, 0);
  lcd.print("Select an option:");
  lcd.setCursor(0, 1);
  lcd.print(menuOptions[selectedOption]);
}
